// Logisim project Proj1313.circ as structural Verilog: 11 circuits, main circuit Arch
module Arch (
  input  [7:0] A,
  input  [7:0] B,
  input  [2:0] opcode,
  output [7:0] O,
  output Cout
);

  ALU alu_1 (.A(A), .B(B), .opcode(opcode), .O(O), .Cout(Cout));
endmodule

module ALU (
  input  [7:0] A,
  input  [7:0] B,
  input  [2:0] opcode,
  output [7:0] O,
  output Cout
);

  wire addr8bit_1_cout, sub8bit_1_cout;
  wire [7:0] addr8bit_1_o, and8bit_1_o, mult8bit_1_o, or8bit_1_o, shift8bit_1_o, sub8bit_1_o, xor8bit_1_o;

  XOR8bit xor8bit_1 (.A(A), .B(B), .O(xor8bit_1_o));
  AND8bit and8bit_1 (.A(A), .B(B), .O(and8bit_1_o));
  OR8bit or8bit_1 (.A(A), .B(B), .O(or8bit_1_o));
  addr8bit addr8bit_1 (.A(A), .B(B), .cin(1'b0), .O(addr8bit_1_o), .cout(addr8bit_1_cout));
  sub8bit sub8bit_1 (.A(A), .B(B), .cin(1'b1), .O(sub8bit_1_o), .Cout(sub8bit_1_cout));
  shift8bit shift8bit_1 (.B(B), .O(shift8bit_1_o));
  Mult8bit mult8bit_1 (.B(B[3:0]), .Cin(1'b0), .A(A[3:0]), .O(mult8bit_1_o));
  Mux8bit8x1 mux8bit8x1_1 (
    .i0(B), .i1(xor8bit_1_o), .i2(and8bit_1_o), .i3(or8bit_1_o), .i4(addr8bit_1_o), .i5(sub8bit_1_o),
    .i6(shift8bit_1_o), .i7(mult8bit_1_o), .opcode(opcode), .O(O));
  Mux1bit8x1 mux1bit8x1_1 (
    .i0(1'b0), .i1(1'b0), .i2(1'b0), .i3(1'b0), .i4(addr8bit_1_cout), .i5(sub8bit_1_cout), .i6(1'b0),
    .i7(1'b0), .s2(opcode[2]), .s1(opcode[1]), .s0(opcode[0]), .O(Cout));
endmodule

module addr8bit (
  input  [7:0] A,
  input  [7:0] B,
  input  cin,
  output [7:0] O,
  output cout
);

  wire addr4bitoa_1_p5;

  // Addr4bitOA addr4bitoa_1: pin names not known; wires that end beside it: A[3:0], B[3:0], cin, O[3:0], addr4bitoa_1_p5
  // Addr4bitOA addr4bitoa_2: pin names not known; wires that end beside it: A[7:4], B[7:4], addr4bitoa_1_p5, O[7:4], cout
endmodule

module shift8bit (
  input  [7:0] B,
  output [7:0] O
);

  wire and_1_out, and_2_out, and_3_out, and_4_out, and_5_out, and_6_out, and_7_out, and_8_out, and_9_out,
       and_10_out, and_11_out, and_12_out, and_13_out, and_14_out, and_15_out, and_16_out;

  and and_1 (and_1_out, 1'b0, 1'b1);
  xor xor_1 (O[7], and_1_out, and_2_out);
  and and_2 (and_2_out, B[7], ~1'b1);  // AND_Gate
  and and_3 (and_3_out, B[7], 1'b1);
  xor xor_2 (O[6], and_3_out, and_4_out);
  and and_4 (and_4_out, B[6], ~1'b1);  // AND_Gate
  and and_5 (and_5_out, B[6], 1'b1);
  xor xor_3 (O[5], and_5_out, and_6_out);
  and and_6 (and_6_out, B[5], ~1'b1);  // AND_Gate
  and and_7 (and_7_out, B[5], 1'b1);
  xor xor_4 (O[4], and_7_out, and_8_out);
  and and_8 (and_8_out, B[4], ~1'b1);  // AND_Gate
  and and_9 (and_9_out, B[4], 1'b1);
  xor xor_5 (O[3], and_9_out, and_10_out);
  and and_10 (and_10_out, B[3], ~1'b1);  // AND_Gate
  and and_11 (and_11_out, B[3], 1'b1);
  xor xor_6 (O[2], and_11_out, and_12_out);
  and and_12 (and_12_out, B[2], ~1'b1);  // AND_Gate
  and and_13 (and_13_out, B[2], 1'b1);
  xor xor_7 (O[1], and_13_out, and_14_out);
  and and_14 (and_14_out, B[1], ~1'b1);  // AND_Gate
  and and_15 (and_15_out, B[1], 1'b1);
  and and_16 (and_16_out, B[0], ~1'b1);  // AND_Gate
  xor xor_8 (O[0], and_15_out, and_16_out);
endmodule

module sub8bit (
  input  [7:0] A,
  input  [7:0] B,
  input  cin,
  output [7:0] O,
  output Cout
);

  wire addr4bitoa_1_p5;
  wire [3:0] not_1_out, not_2_out;

  assign not_1_out = ~B[3:0];  // NOT_Gate not_1, 4 bits wide
  assign not_2_out = ~B[7:4];  // NOT_Gate not_2, 4 bits wide
  // Addr4bitOA addr4bitoa_1: pin names not known; wires that end beside it: A[3:0], not_1_out, cin, O[3:0], addr4bitoa_1_p5
  // Addr4bitOA addr4bitoa_2: pin names not known; wires that end beside it: not_2_out, addr4bitoa_1_p5, A[7:4], O[7:4], Cout
endmodule

module XOR8bit (
  input  [7:0] A,
  input  [7:0] B,
  output [7:0] O
);

  xor xor_1 (O[0], A[0], B[0]);
  xor xor_2 (O[1], A[1], B[1]);
  xor xor_3 (O[2], A[2], B[2]);
  xor xor_4 (O[3], A[3], B[3]);
  xor xor_5 (O[4], A[4], B[4]);
  xor xor_6 (O[5], A[5], B[5]);
  xor xor_7 (O[6], A[6], B[6]);
  xor xor_8 (O[7], A[7], B[7]);
endmodule

module AND8bit (
  input  [7:0] A,
  input  [7:0] B,
  output [7:0] O
);

  and and_1 (O[0], A[0], B[0]);
  and and_2 (O[1], A[1], B[1]);
  and and_3 (O[2], A[2], B[2]);
  and and_4 (O[3], A[3], B[3]);
  and and_5 (O[4], A[4], B[4]);
  and and_6 (O[5], A[5], B[5]);
  and and_7 (O[6], A[6], B[6]);
  and and_8 (O[7], A[7], B[7]);
endmodule

module OR8bit (
  input  [7:0] A,
  input  [7:0] B,
  output [7:0] O
);

  or or_1 (O[0], A[0], B[0]);
  or or_2 (O[1], A[1], B[1]);
  or or_3 (O[2], A[2], B[2]);
  or or_4 (O[3], A[3], B[3]);
  or or_5 (O[4], A[4], B[4]);
  or or_6 (O[5], A[5], B[5]);
  or or_7 (O[6], A[6], B[6]);
  or or_8 (O[7], A[7], B[7]);
endmodule

module Mux1bit8x1 (
  input  i0,
  input  i1,
  input  i2,
  input  i3,
  input  i4,
  input  i5,
  input  i6,
  input  i7,
  input  s2,
  input  s1,
  input  s0,
  output O
);

  wire and_1_out, and_2_out, and_3_out, and_4_out, and_5_out, and_6_out, and_7_out, and_8_out;

  and and_1 (and_1_out, i0, ~s2, ~s1, ~s0);  // AND_Gate
  and and_2 (and_2_out, i1, ~s2, ~s1, s0);  // AND_Gate
  and and_3 (and_3_out, i2, ~s2, s1, ~s0);  // AND_Gate
  and and_4 (and_4_out, i3, ~s2, s1, s0);  // AND_Gate
  and and_5 (and_5_out, i4, s2, ~s1, ~s0);  // AND_Gate
  and and_6 (and_6_out, i5, s2, ~s1, s0);  // AND_Gate
  and and_7 (and_7_out, i6, s2, s1, ~s0);  // AND_Gate
  and and_8 (and_8_out, i7, s2, s1, s0);
  or or_1 (O, and_1_out, and_2_out, and_3_out, and_4_out, and_5_out, and_6_out, and_7_out, and_8_out);
endmodule

module Mux8bit8x1 (
  input  [7:0] i0,
  input  [7:0] i1,
  input  [7:0] i2,
  input  [7:0] i3,
  input  [7:0] i4,
  input  [7:0] i5,
  input  [7:0] i6,
  input  [7:0] i7,
  input  [2:0] opcode,
  output [7:0] O
);

  Mux1bit8x1 Out0 (
    .i0(i0[0]), .i1(i1[0]), .i2(i2[0]), .i3(i3[0]), .i4(i4[0]), .i5(i5[0]), .i6(i6[0]), .i7(i7[0]),
    .s2(opcode[2]), .s1(opcode[1]), .s0(opcode[0]), .O(O[0]));
  Mux1bit8x1 Out1 (
    .i0(i0[1]), .i1(i1[1]), .i2(i2[1]), .i3(i3[1]), .i4(i4[1]), .i5(i5[1]), .i6(i6[1]), .i7(i7[1]),
    .s2(opcode[2]), .s1(opcode[1]), .s0(opcode[0]), .O(O[1]));
  Mux1bit8x1 Out2 (
    .i0(i0[2]), .i1(i1[2]), .i2(i2[2]), .i3(i3[2]), .i4(i4[2]), .i5(i5[2]), .i6(i6[2]), .i7(i7[2]),
    .s2(opcode[2]), .s1(opcode[1]), .s0(opcode[0]), .O(O[2]));
  Mux1bit8x1 Out3 (
    .i0(i0[3]), .i1(i1[3]), .i2(i2[3]), .i3(i3[3]), .i4(i4[3]), .i5(i5[3]), .i6(i6[3]), .i7(i7[3]),
    .s2(opcode[2]), .s1(opcode[1]), .s0(opcode[0]), .O(O[3]));
  Mux1bit8x1 Out4 (
    .i0(i0[4]), .i1(i1[4]), .i2(i2[4]), .i3(i3[4]), .i4(i4[4]), .i5(i5[4]), .i6(i6[4]), .i7(i7[4]),
    .s2(opcode[2]), .s1(opcode[1]), .s0(opcode[0]), .O(O[4]));
  Mux1bit8x1 Out5 (
    .i0(i0[5]), .i1(i1[5]), .i2(i2[5]), .i3(i3[5]), .i4(i4[5]), .i5(i5[5]), .i6(i6[5]), .i7(i7[5]),
    .s2(opcode[2]), .s1(opcode[1]), .s0(opcode[0]), .O(O[5]));
  Mux1bit8x1 Out6 (
    .i0(i0[6]), .i1(i1[6]), .i2(i2[6]), .i3(i3[6]), .i4(i4[6]), .i5(i5[6]), .i6(i6[6]), .i7(i7[6]),
    .s2(opcode[2]), .s1(opcode[1]), .s0(opcode[0]), .O(O[6]));
  Mux1bit8x1 Out7 (
    .i0(i0[7]), .i1(i1[7]), .i2(i2[7]), .i3(i3[7]), .i4(i4[7]), .i5(i5[7]), .i6(i6[7]), .i7(i7[7]),
    .s2(opcode[2]), .s1(opcode[1]), .s0(opcode[0]), .O(O[7]));
endmodule

module Mult8bit (
  input  [3:0] B,
  input  Cin,
  input  [3:0] A,
  output [7:0] O
);

  wire [2:0] and_15_out;
  wire [3:0] addr4bitoa_1_p4, and_10_out, and_11_out, and_12_out;
  wire [3:1] addr4bitoa_3_p1;
  wire [3:3] addr4bitoa_2_p3;

  and and_1 (and_11_out[3], A[1], B[3]);
  and and_2 (and_10_out[3], A[3], B[3]);
  and and_3 (and_11_out[2], A[1], B[2]);
  and and_4 (and_12_out[3], A[2], B[3]);
  and and_5 (and_12_out[2], A[2], B[2]);
  and and_6 (and_10_out[2], A[3], B[2]);
  and and_7 (and_11_out[1], A[1], B[1]);
  and and_8 (and_12_out[1], A[2], B[1]);
  and and_9 (and_10_out[1], A[3], B[1]);
  and and_10 (and_10_out[0], A[3], B[0]);
  and and_11 (and_11_out[0], A[1], B[0]);
  and and_12 (and_12_out[0], A[2], B[0]);
  and and_13 (and_15_out[2], A[0], B[3]);
  and and_14 (and_15_out[1], A[0], B[2]);
  and and_15 (and_15_out[0], A[0], B[1]);
  // Addr4bitOA addr4bitoa_1: pin names not known; wires that end beside it: {Cin, and_15_out}, and_11_out, Cin, {addr4bitoa_1_p4[2:0], O[1]}, addr4bitoa_1_p4[3]
  // Addr4bitOA addr4bitoa_2: pin names not known; wires that end beside it: and_12_out, Cin, addr4bitoa_2_p3[3]
  // Addr4bitOA addr4bitoa_3: pin names not known; wires that end beside it: {addr4bitoa_2_p3[3], addr4bitoa_3_p1}, and_10_out, Cin, O[7]
  and and_16 (O[0], A[0], B[0]);
endmodule
