// Logisim project logisimtutorial.circ as structural Verilog: 4 circuits, main circuit main
module main (
  input  in_1,
  output out_2
);
endmodule

module FullAddr_1bitOA (
  input  a,
  input  b,
  input  ci,
  output co,
  output SumOA
);

  wire and_1_out, and_2_out, and_3_out, and_4_out, and_5_out, and_6_out, and_7_out;

  and and_1 (and_1_out, a, ci);
  and and_2 (and_2_out, b, ci);
  and and_3 (and_3_out, a, b);
  and and_4 (and_4_out, ~a, ~ci, b);  // AND_Gate
  and and_5 (and_5_out, ~ci, a, ~b);  // AND_Gate
  and and_6 (and_6_out, ci, ~a, ~b);  // AND_Gate
  and and_7 (and_7_out, ci, a, b);
  or or_1 (co, and_1_out, and_2_out, and_3_out);
  or or_2 (SumOA, and_4_out, and_5_out, and_6_out, and_7_out);
endmodule

module Addr4bitOA (
  input  [3:0] a,
  input  [3:0] b,
  input  cin,
  output [3:0] SumOA,
  output cout
);

  wire fulladdr_1bitoa_1_co, fulladdr_1bitoa_2_co, fulladdr_1bitoa_3_co;

  FullAddr_1bitOA fulladdr_1bitoa_1 (.a(a[0]), .b(b[0]), .ci(cin), .co(fulladdr_1bitoa_1_co), .SumOA(SumOA[0]));
  FullAddr_1bitOA fulladdr_1bitoa_2 (
    .a(a[1]), .b(b[1]), .ci(fulladdr_1bitoa_1_co), .co(fulladdr_1bitoa_2_co), .SumOA(SumOA[1]));
  FullAddr_1bitOA fulladdr_1bitoa_3 (
    .a(a[2]), .b(b[2]), .ci(fulladdr_1bitoa_2_co), .co(fulladdr_1bitoa_3_co), .SumOA(SumOA[2]));
  FullAddr_1bitOA fulladdr_1bitoa_4 (.a(a[3]), .b(b[3]), .ci(fulladdr_1bitoa_3_co), .co(cout), .SumOA(SumOA[3]));
endmodule

module Sub4bitOA (
  input  [3:0] a,
  input  [3:0] b,
  input  cin,
  output [3:0] DiffOA,
  output cout
);

  wire fulladdr_1bitoa_1_co, fulladdr_1bitoa_2_co, fulladdr_1bitoa_3_co, not_1_out, not_2_out, not_3_out,
       not_4_out;

  not not_1 (not_1_out, b[0]);
  not not_2 (not_2_out, b[1]);
  not not_3 (not_3_out, b[2]);
  not not_4 (not_4_out, b[3]);
  FullAddr_1bitOA fulladdr_1bitoa_1 (.a(a[0]), .b(not_1_out), .ci(cin), .co(fulladdr_1bitoa_1_co), .SumOA(DiffOA[0]));
  FullAddr_1bitOA fulladdr_1bitoa_2 (
    .a(a[1]), .b(not_2_out), .ci(fulladdr_1bitoa_1_co), .co(fulladdr_1bitoa_2_co), .SumOA(DiffOA[1]));
  FullAddr_1bitOA fulladdr_1bitoa_3 (
    .a(a[2]), .b(not_3_out), .ci(fulladdr_1bitoa_2_co), .co(fulladdr_1bitoa_3_co), .SumOA(DiffOA[2]));
  FullAddr_1bitOA fulladdr_1bitoa_4 (.a(a[3]), .b(not_4_out), .ci(fulladdr_1bitoa_3_co), .co(cout), .SumOA(DiffOA[3]));
endmodule
